# Fritzing sketch blade-wiring (saved by Fritzing 0.9.3b)

parts:
  Raspberry_Pi_1 = Raspberry Pi 3 [part_number=RPI-3-V1.2]
  Lisiparoi2 = Lisiparoi v1.0 Infra Red

nets:
  N1: Raspberry_Pi_1.GPIO2, Lisiparoi2.GPIO
  GND: Raspberry_Pi_1.GND, Lisiparoi2.GND1
  5V: Raspberry_Pi_1.5V, Lisiparoi2.5V

custom parts:
  Lisiparoi v1.0 Infra Red: Infra Red LED halo for Raspberry Pi Camera
